// Logisim project 4bitALU.circ as structural Verilog: 1 circuit, main circuit main
module main (
  input  A0,
  input  B0,
  input  Sub,
  input  A1,
  input  B1,
  input  [1:0] op,
  input  A2,
  input  B2,
  input  A3,
  input  B3,
  output out_11,
  output out_12,
  output out_13,
  output Cout,
  output out_15
);

  wire and_1_out, and_2_out, and_3_out, and_4_out, and_5_out, and_6_out, and_7_out, and_8_out, and_9_out,
       and_10_out, and_11_out, and_12_out, or_1_out, or_2_out, or_3_out, or_5_out, or_6_out, or_7_out,
       or_8_out, xor_1_out, xor_2_out, xor_3_out, xor_4_out, xor_5_out, xor_6_out, xor_7_out, xor_8_out,
       xor_9_out, xor_10_out, xor_11_out, xor_12_out;

  xor xor_1 (xor_1_out, B0, Sub);
  xor xor_2 (xor_2_out, B1, Sub);
  xor xor_3 (xor_3_out, B2, Sub);
  xor xor_4 (xor_4_out, B3, Sub);
  and and_1 (and_1_out, A0, xor_1_out);
  xor xor_5 (xor_5_out, A0, xor_1_out);
  and and_2 (and_2_out, A1, xor_2_out);
  xor xor_6 (xor_6_out, A1, xor_2_out);
  and and_3 (and_3_out, A2, xor_3_out);
  xor xor_7 (xor_7_out, A2, xor_3_out);
  and and_4 (and_4_out, A3, xor_4_out);
  xor xor_8 (xor_8_out, A3, xor_4_out);
  and and_5 (and_5_out, xor_5_out, Sub);
  xor xor_9 (xor_9_out, xor_5_out, Sub);
  and and_6 (and_6_out, xor_6_out, or_1_out);
  xor xor_10 (xor_10_out, xor_6_out, or_1_out);
  and and_7 (and_7_out, xor_7_out, or_2_out);
  xor xor_11 (xor_11_out, xor_7_out, or_2_out);
  and and_8 (and_8_out, xor_8_out, or_3_out);
  xor xor_12 (xor_12_out, xor_8_out, or_3_out);
  or or_1 (or_1_out, and_1_out, and_5_out);
  or or_2 (or_2_out, and_2_out, and_6_out);
  or or_3 (or_3_out, and_3_out, and_7_out);
  or or_4 (Cout, and_4_out, and_8_out);
  and and_9 (and_9_out, A0, B0);
  or or_5 (or_5_out, A0, B0);
  and and_10 (and_10_out, A1, B1);
  or or_6 (or_6_out, A1, B1);
  and and_11 (and_11_out, A2, B2);
  or or_7 (or_7_out, A2, B2);
  and and_12 (and_12_out, A3, B3);
  or or_8 (or_8_out, A3, B3);
  Multiplexer #(.select(2)) multiplexer_1 (
    .in0(xor_9_out), .in1(and_9_out), .in2(or_5_out), .out(out_11), .sel(op));  // open: in3
  Multiplexer #(.select(2)) multiplexer_2 (
    .in0(xor_10_out), .in1(and_10_out), .in2(or_6_out), .out(out_12), .sel(op));  // open: in3
  Multiplexer #(.select(2)) multiplexer_3 (
    .in0(xor_11_out), .in1(and_11_out), .in2(or_7_out), .out(out_13), .sel(op));  // open: in3
  Multiplexer #(.select(2)) multiplexer_4 (
    .in0(xor_12_out), .in1(and_12_out), .in2(or_8_out), .out(out_15), .sel(op));  // open: in3
endmodule
